# Fritzing sketch MultiFlash FM0X (saved by Fritzing 0.9.4)
breadboards: 1

parts:
  Part1 = Adafruit Feather M0 Express [part_number="Adafruit #3403"]
  Part2 = Adafruit OLED FeatherWing [part_number="Adafruit #2900"]
  C1 = Capacitor Polarized [package=cpol-radial-100uf-25v]
  C2 = Capacitor Polarized [package=cpol-radial-100uf-25v]
  S1 = Toggle Switch [package=THT]

nets:
  GND: Part1.GND, Part2.GND, C1.-, C2.-
  +3V3: Part1.+3V3, Part2.3.3V, C1.+, C2.+, S1.COM
  N1: Part1.D9, Part2.J
  N2: Part1.D6, Part2.I
  N3: Part1.D5, Part2.H
  N4: Part1.SCL, Part2.SCL
  N5: Part1.SDA, Part2.SDA

notes:
  SWDIO
  SWCLK
  RESET
  GND
  3V3

custom parts:
  Adafruit Feather M0 Express: We love all our Feathers equally, but this Feather is very special. It's our first Feather that is specifically designed for use with CircuitPython! CircuitPython is our beginner-oriented flavor of MicroPython - and as the name hints at, its a small but full-featured version of the popular Python programming language specifically for use with circuitry and electronics. That doesn't mean you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
  Adafruit OLED FeatherWing: This is the FeatherWing OLED: it adds a 128x32 monochrome OLED plus 3 user buttons to any Feather main board. These displays are small, only about 1" diagonal, but very readable due to the high contrast of an OLED display. This screen is made of 128x32 individual white OLED pixels and because the display makes its own light, no backlight is required. This reduces the power required to run the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
